# Fritzing sketch SmartGarden (saved by Fritzing 1.0.5)
breadboards: 1

parts:
  M1 = HTU21d
  Part2 = FC-28 Soil Hygrometer Module - Probe
  Part3 = FC-28 Soil Hygrometer Module
  WATER_PUMP1 = water pump/motor  # not connected
  Part4 = IFR520 MOS module [package=THT]
  VCC2 = 4 x AAA Battery Mount [internal_resistance=0.1Ω]
  U3 = Mini-360 DC-DC Buck converter [package=THT]
  esp1 = ESP32 DevKitc V4
  Part5 = BH1750
  Sensor1 = Gas Sensor Breakout Board
  U4 = HC-SR04 [chip_label=IC package="SIP (Single Inline) [THT]"]
  R1 = Resistor [tolerance=±5% power=0.25W resistance=2.2k package=THT]
  R2 = Resistor [tolerance=±5% power=0.25W resistance=2.2k package=THT]  # not connected

nets:
  VCC: M1.VIN, Part3.VCC, esp1.3V3, Part5.VCC
  GND: M1.GND, Part3.GND, esp1.GND#18, Part5.GND, Sensor1.GND, U4.GND
  N1: M1.SCL, esp1.IO22, Part5.SCL
  N2: M1.SDA, esp1.IO21, Part5.SDA
  N3: Part2.POS, Part3.POS
  N4: Part2.NEG, Part3.NEG
  N5: Part3.AO, esp1.IO34
  N6: Part4.SIG, esp1.IO18
  VCC_2: Part4.VCC, VCC2.+, U3.IN+, esp1.5V, Sensor1.5V, U4.Vcc
  N7: Part4.GND, VCC2.-, U3.IN-, U3.OUT-, esp1.GND#12
  N8: Part4.VIN, U3.OUT+
  N9: esp1.IO35, Sensor1.AOUT
  N10: esp1.IO12, R1.Pin_1
  N11: esp1.IO13, U4.Trig
  N12: U4.Echo, R1.Pin_0

custom parts:
  HTU21d: Temperature Humidity Sensor, I2C
  FC-28 Soil Hygrometer Module - Probe: The FC-28 is a soil hygrometer module that uses the Texas Instruments LM393 comparator chip to provide an analog measurement of soil humidity.
  FC-28 Soil Hygrometer Module: The FC-28 is a soil hygrometer module that uses the Texas Instruments LM393 comparator chip to provide an analog measurement of soil humidity. The digital output is high when soil moisture is over a certain threshold, as determined by adjusting the potentiometer.
  water pump/motor: WATER PUMP BY ARDUBLOCKTR
  IFR520 MOS module: Breakout board for the IFR520 MOSFET transistor. The module is designed to switch heavy DC loads from a single digital pin of your microcontroller. Its main purpose is to provide a low cost way to drive a DC motor for robotics applications, but the module can be used to control most high current DC loads. Screw terminals are provided to interface to your load and external power source. An LED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
  Mini-360 DC-DC Buck converter: Mini-360 DC-DC Buck converter. Tiny buck step down voltage converter, input voltage 4.75 to 23V output 1 to 17V adjustable. Available from ebay and the like.
  ESP32 DevKitc V4: ESP32-DevKitC board with ESP32-WROOM-32 module. ESP32-DevKitC V4 is a small-sized ESP32-based development board produced by Espressif. Most of the pins on the ESP module are broken out to the pin headers on the board. The pins D0, D1, D2, D3, CMD and CLK are used internally for communication between ESP32 and SPI flash memory. They are grouped on both sides near the USB connector. Avoid using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
  BH1750: Light Sensor
  Gas Sensor Breakout Board: Gas sensor breakout board. Input voltage is 5V. Sensor output is available in analog and digital.
  HC-SR04: HC-SR04 ultrasound distance sensor
